# Fritzing sketch circuitDiagram (saved by Fritzing 0.9.3b)
breadboards: 1

parts:
  U1 = NodeMCU V1.0
  J1 = Basic Servo
  U2 = LCD-16X2 [package=lcd-16x2_noholes]  # not connected
  Part2 = KY-037 High Sensitivity Sound Detection Module [package="Breakout board"]
  Part3 = RFID-RC522-v2

nets:
  N1: U1.D3, J1.pulse
  N2: U1.D4, Part3.RST
  3V3: U1.3V3, J1.vcc, Part2.+, Part3.3_3V
  GND: U1.GND, J1.gnd, Part2.G, Part3.GND
  N3: U1.D5, Part3.SCK
  N4: U1.D6, Part3.MISO
  N5: U1.D7, Part3.MOSI
  N6: U1.D8, Part3.SDA
  N7: U1.A0, Part2.A0

custom parts:
  NodeMCU V1.0: ESP8266 based NodeMCU
  KY-037 High Sensitivity Sound Detection Module: KY-037 high sensitivity sound detection module is an analog/digital sensor that uses a condenser microphone to observe changes in environment noise.
  RFID-RC522-v2: A simple China made RFID-RC522 Reader; do check the pin labels, as this is a MFRC522 based clone.
